# Fritzing sketch TH_Monitor_schematic (saved by Fritzing 0.9.3b)
breadboards: 1

parts:
  LED1 = RGB LED - (4 legs) [package="5 mm [THT]"]
  R1 = Resistor [tolerance=±5% resistance=140 package="0603 [SMD]"]
  R2 = Resistor [tolerance=±5% resistance=100 package="0603 [SMD]"]
  R3 = Resistor [tolerance=±5% resistance=100 package="0603 [SMD]"]
  microSD1 = MicroSD Card Module
  Componente1 = Arduino Nano (Rev3.0) (ICSP)
  OLED_I2C1 = OLED 128x64 I2C Monochrome Display
  S1 = Pushbutton [package="[SMD]"]
  Mod1 = KY-015 Temperature & Humidity Sensor Module [package="Breakout board"]

nets:
  N1: LED1.red_cathode, R1.Pin_0
  VCC: LED1.common_anode, microSD1.VCC, Componente1.5V, OLED_I2C1.VDD, Mod1.S
  N2: LED1.green_cathode, R2.Pin_0
  N3: LED1.blue_cathode, R3.Pin_0
  N4: R1.Pin_1, Componente1.D3
  N5: R2.Pin_1, Componente1.D5
  N6: R3.Pin_1, Componente1.D6
  GND: microSD1.GND, Componente1.GND, OLED_I2C1.GND, S1.Pin_3, S1.Pin_4, Mod1.-
  N7: microSD1.MISO, Componente1.D12/MISO
  N8: microSD1.MOSI, Componente1.D11/MOSI
  N9: microSD1.SCK, Componente1.D13/SCK
  N10: microSD1.CS, Componente1.D10
  N11: Componente1.D2, Mod1.Vin
  N12: Componente1.D4, S1.Pin_1, S1.Pin_2
  N13: Componente1.A5, OLED_I2C1.SCK
  N14: Componente1.A4, OLED_I2C1.SDA

custom parts:
  KY-015 Temperature & Humidity Sensor Module: KY-015 temperature and humidity sensor module, provides a low-latency serial interface to measure humidity and temperature.
